# Fritzing sketch semu (saved by Fritzing 0.9.3b)
breadboards: 1

parts:
  hc-sr1 = hc-sr04
  J1 = Basic Servo
  Part1 = Arduino Uno (Rev3)

nets:
  VCC: hc-sr1.VCC, J1.vcc, Part1.5V
  N1: hc-sr1.Trig, Part1.D5_PWM
  N2: hc-sr1.Echo, Part1.D6_PWM
  GND: hc-sr1.GND, J1.gnd, Part1.GND

// code stored in the sketch: Untitled.ino
#include<Servo.h>
Servo myservo;
int pos=20;
const int trigpin=5;
const int echopin=6;


long duration;
float distance;


void setup()
{
  myservo.attach(11);
  pinMode(trigpin,OUTPUT);
  pinMode(echopin,INPUT);

  myservo.write(pos);
  
  
}
void loop()
{
  //serial.begin(9600);
  digitalWrite(trigpin,LOW);
  delayMicroseconds(1);
  digitalWrite(trigpin,HIGH);
  delayMicroseconds(1000);
digitalWrite(trigpin,LOW);
  duration=pulseIn(echopin,HIGH);
  distance=0.034*(duration/2);
  //serial.println(distance);
  if(distance<10)
  {
    myservo.write(pos+160);
    delay(3000);
    
  }
  else
  {
    myservo.write(pos);
   
  }
  delay(1000);
}
